# Fritzing sketch Gardbot (saved by Fritzing 0.9.3b)
circuit board: 8.46667cm x 5.64444cm
breadboards: 1

parts:
  Real_Time_Clock = DS1302 [package="SO8 [SMD]"]
  Arduino = Arduino Mega 2560 (Rev3)
  SD_Card_Reader = MicroSD Card Module
  Buzzer = Piezo Speaker
  R1_-_Buzzer = Resistor [tolerance=±1% resistance=10k package=THT]
  R2_-_DHT11 = Resistor [tolerance=±5% resistance=100 package="0603 [SMD]"]
  DHT11_-_Temp_Hum = Humidity and Temperature Sensor RHT03

nets:
  VCC: Real_Time_Clock.+V, Arduino.5V, SD_Card_Reader.VCC, R2_-_DHT11.Pin_0, DHT11_-_Temp_Hum.Vcc
  GND: Real_Time_Clock.0V, Arduino.GND, SD_Card_Reader.GND, Buzzer.pin1, DHT11_-_Temp_Hum.GND_2
  N1: Real_Time_Clock.CE_-_Chip_Enable, Arduino.D5_PWM
  N2: Real_Time_Clock.I/O_-_SPI_Data_In/Out, Arduino.D6_PWM
  N3: Real_Time_Clock.SCLK_-_SPI_Clock, Arduino.D7_PWM
  N4: Arduino.D3_PWM, R1_-_Buzzer.Pin_0
  N5: Arduino.D22, R2_-_DHT11.Pin_1, DHT11_-_Temp_Hum.Data-signal
  N6: Arduino.D50, SD_Card_Reader.MISO
  N7: Arduino.D51, SD_Card_Reader.MOSI
  N8: Arduino.D52, SD_Card_Reader.SCK
  N9: Arduino.D53, SD_Card_Reader.CS
  N10: Buzzer.pin2, R1_-_Buzzer.Pin_1
